// Logisim project lcd.circ as structural Verilog: 7 circuits, main circuit main
module main (
  input  [3:0] in_1,
  input  [3:0] in_2,
  input  [1:0] in_3,
  output [3:0] out_4,
  output [3:0] out_5
);

  wire [1:0] undriven;
  wire [3:0] adder_1_out, adder_2_out, and_1_out, or_1_out, subtractor_1_out, subtractor_2_out, xnor_1_out,
       xor_1_out;

  Adder_part #(.width(4)) adder_1 (.a(in_1), .b(4'b0001), .out(adder_1_out));  // open: cin, cout
  Adder_part #(.width(4)) adder_2 (.a(in_1), .b(in_2), .out(adder_2_out));  // open: cin, cout
  Subtractor_part #(.width(4)) subtractor_1 (.a(in_1), .b(in_2), .out(subtractor_1_out));  // open: bin, bout
  Subtractor_part #(.width(4)) subtractor_2 (.a(in_1), .b(in_2), .out(subtractor_2_out));  // open: bin, bout
  assign and_1_out = in_1 & in_2;  // AND_Gate and_1, 4 bits wide
  assign or_1_out = in_1 | in_2;  // OR_Gate or_1, 4 bits wide
  assign xor_1_out = in_1 ^ in_2;  // XOR_Gate xor_1, 4 bits wide
  assign xnor_1_out = ~(in_1 ^ in_2);  // XNOR_Gate xnor_1, 4 bits wide
  Multiplexer #(.select(2), .width(4)) multiplexer_1 (
    .in1(and_1_out), .in2(or_1_out), .in3(xor_1_out), .out(out_4), .sel(undriven));  // open: in0, en
  Multiplexer #(.select(2), .width(4)) multiplexer_2 (
    .in1(adder_1_out), .in2(adder_2_out), .in3(subtractor_1_out), .out(out_5));  // open: in0, sel, en
endmodule

module Adder (
  input  [3:0] in_1,
  input  [3:0] in_2,
  input  [3:0] Carry_in,
  output [3:0] out_4,
  output [3:0] Carry_out
);

  wire [3:0] and_1_out, and_2_out, undriven;

  assign Carry_in = in_1 ^ in_2;  // XOR_Gate xor_1, 4 bits wide
  assign and_1_out = in_2 & in_1;  // AND_Gate and_1, 4 bits wide
  assign and_2_out = undriven & Carry_in;  // AND_Gate and_2, 4 bits wide
  assign out_4 = Carry_in ^ undriven;  // XOR_Gate xor_2, 4 bits wide
  assign Carry_out = and_2_out | and_1_out;  // OR_Gate or_1, 4 bits wide
endmodule

module Subtractor (
  input  [3:0] in_1,
  input  [3:0] in_2,
  input  [3:0] in_3,
  output [3:0] out_4,
  output [3:0] out_5
);

  wire [3:0] and_1_out, and_2_out, not_1_out, xor_1_out;

  assign not_1_out = ~in_2;  // NOT_Gate not_1, 4 bits wide
  assign xor_1_out = in_1 ^ not_1_out;  // XOR_Gate xor_1, 4 bits wide
  assign and_1_out = not_1_out & in_1;  // AND_Gate and_1, 4 bits wide
  assign and_2_out = in_3 & xor_1_out;  // AND_Gate and_2, 4 bits wide
  assign out_4 = xor_1_out ^ in_3;  // XOR_Gate xor_2, 4 bits wide
  assign out_5 = and_2_out | and_1_out;  // OR_Gate or_1, 4 bits wide
endmodule

module ALU (
  input  [3:0] in_1,
  input  [3:0] in_2,
  output [3:0] out_3
);

  wire bcd_1_a, bcd_1_b, bcd_1_c, bcd_1_d, bcd_1_e, bcd_1_f, bcd_1_g;
  wire [1:0] undriven;
  wire [3:0] arithmetic_1_out_4, logic_1_out_4;

  Logic logic_1 (.in_1(in_1), .in_2(in_2), .in_3(undriven), .out_4(logic_1_out_4));
  Arithmetic arithmetic_1 (.in_1(in_1), .in_2(in_2), .in_3(undriven), .out_4(arithmetic_1_out_4));
  Multiplexer #(.width(4), .enable("false")) multiplexer_1 (
    .in0(logic_1_out_4), .in1(arithmetic_1_out_4), .out(out_3));  // open: sel
  BCD bcd_1 (
    .D0(arithmetic_1_out_4[0]), .D1(arithmetic_1_out_4[1]), .D2(arithmetic_1_out_4[2]),
    .D3(arithmetic_1_out_4[3]), .a(bcd_1_a), .b(bcd_1_b), .c(bcd_1_c), .d(bcd_1_d), .e(bcd_1_e), .f(bcd_1_f),
    .g(bcd_1_g));
  _7_Segment_Display u_7_segment_display_1 (
    .g(bcd_1_g), .f(bcd_1_f), .a(bcd_1_a), .b(bcd_1_b), .e(bcd_1_e), .d(bcd_1_d), .c(bcd_1_c));  // open: dp
  LED led_1 (.in(logic_1_out_4[0]));
  LED led_2 (.in(logic_1_out_4[1]));
  LED led_3 (.in(logic_1_out_4[2]));
  LED led_4 (.in(logic_1_out_4[3]));
endmodule

module Logic (
  input  [3:0] in_1,
  input  [3:0] in_2,
  input  [1:0] in_3,
  output [3:0] out_4
);

  wire [1:0] undriven;
  wire [3:0] and_1_out, or_1_out, xnor_1_out, xor_1_out;

  assign and_1_out = in_1 & in_2;  // AND_Gate and_1, 4 bits wide
  assign or_1_out = in_1 | in_2;  // OR_Gate or_1, 4 bits wide
  assign xor_1_out = in_1 ^ in_2;  // XOR_Gate xor_1, 4 bits wide
  assign xnor_1_out = ~(in_1 ^ in_2);  // XNOR_Gate xnor_1, 4 bits wide
  Multiplexer #(.select(2), .width(4), .enable("false")) multiplexer_1 (
    .in1(and_1_out), .in2(or_1_out), .in3(xor_1_out), .out(out_4), .sel(undriven));  // open: in0
endmodule

module Arithmetic (
  input  [3:0] in_1,
  input  [3:0] in_2,
  input  [1:0] in_3,
  output [3:0] out_4
);

  wire [1:0] undriven;
  wire [3:0] adder_1_out, adder_2_out, subtractor_1_out, subtractor_2_out;

  Adder_part #(.width(4)) adder_1 (.a(in_1), .b(4'b0001), .out(adder_1_out));  // open: cin, cout
  Adder_part #(.width(4)) adder_2 (.a(in_1), .b(in_2), .out(adder_2_out));  // open: cin, cout
  Subtractor_part #(.width(4)) subtractor_1 (.a(in_1), .b(in_2), .out(subtractor_1_out));  // open: bin, bout
  Subtractor_part #(.width(4)) subtractor_2 (.a(in_2), .b(in_1), .out(subtractor_2_out));  // open: bin, bout
  Multiplexer #(.select(2), .width(4), .enable("false")) multiplexer_1 (
    .in1(adder_1_out), .in2(adder_2_out), .in3(subtractor_1_out), .out(out_4), .sel(undriven));  // open: in0
endmodule

module BCD (
  input  D0,
  input  D1,
  input  D2,
  input  D3,
  output a,
  output b,
  output c,
  output d,
  output e,
  output f,
  output g
);

  wire and_1_out, and_2_out, and_3_out, and_4_out, and_5_out, and_6_out, and_7_out, and_8_out, and_9_out,
       and_10_out, and_11_out, and_12_out, and_13_out, and_14_out, and_15_out, and_16_out, and_17_out,
       and_18_out, and_19_out, and_20_out, not_1_out, not_2_out, not_3_out, not_4_out, not_5_out, not_6_out,
       not_7_out, not_8_out, not_9_out, not_10_out, not_11_out, not_12_out, not_13_out, not_14_out,
       not_15_out, not_16_out, not_17_out, not_18_out, not_19_out, not_20_out, not_21_out, not_22_out,
       or_1_out, or_2_out, or_3_out, or_4_out, or_6_out, or_8_out, or_9_out, or_12_out, or_13_out, or_14_out,
       or_15_out;

  not not_1 (not_1_out, D1);
  and and_1 (and_1_out, not_1_out, not_2_out);
  not not_2 (not_2_out, D3);
  and and_2 (and_2_out, D1, D3);
  not not_3 (not_3_out, D1);
  not not_4 (not_4_out, D2);
  and and_3 (and_3_out, not_4_out, not_5_out);
  not not_5 (not_5_out, D3);
  not not_6 (not_6_out, D2);
  or or_1 (or_1_out, not_6_out, D3);
  not not_7 (not_7_out, D1);
  and and_4 (and_4_out, not_7_out, not_8_out);
  not not_8 (not_8_out, D3);
  not not_9 (not_9_out, D1);
  and and_5 (and_5_out, not_9_out, D2);
  not not_10 (not_10_out, D3);
  and and_6 (and_6_out, D1, not_11_out);
  not not_11 (not_11_out, D2);
  not not_12 (not_12_out, D1);
  and and_7 (and_7_out, not_12_out, not_13_out);
  not not_13 (not_13_out, D3);
  and and_8 (and_8_out, D2, not_14_out);
  not not_14 (not_14_out, D3);
  not not_15 (not_15_out, D1);
  and and_9 (and_9_out, not_15_out, not_16_out);
  not not_16 (not_16_out, D2);
  not not_17 (not_17_out, D3);
  and and_10 (and_10_out, D1, not_18_out);
  not not_18 (not_18_out, D2);
  and and_11 (and_11_out, D1, D2);
  not not_19 (not_19_out, D3);
  not not_20 (not_20_out, D1);
  and and_12 (and_12_out, not_20_out, D2);
  and and_13 (and_13_out, D1, not_21_out);
  not not_21 (not_21_out, D2);
  and and_14 (and_14_out, D1, not_22_out);
  not not_22 (not_22_out, D3);
  or or_2 (or_2_out, and_1_out, D2);
  or or_3 (or_3_out, and_2_out, D0);
  or or_4 (or_4_out, not_3_out, and_3_out);
  and and_15 (and_15_out, D2, D3);
  or or_5 (c, or_1_out, D1);
  or or_6 (or_6_out, and_4_out, and_5_out);
  and and_16 (and_16_out, D2, not_10_out);
  and and_17 (and_17_out, and_6_out, D3);
  or or_7 (e, and_7_out, and_8_out);
  and and_18 (and_18_out, and_9_out, not_17_out);
  and and_19 (and_19_out, and_10_out, D3);
  and and_20 (and_20_out, and_11_out, not_19_out);
  or or_8 (or_8_out, and_12_out, and_13_out);
  or or_9 (or_9_out, and_14_out, D0);
  or or_10 (a, or_2_out, or_3_out);
  or or_11 (b, or_4_out, and_15_out);
  or or_12 (or_12_out, or_6_out, and_16_out);
  or or_13 (or_13_out, and_17_out, D0);
  or or_14 (or_14_out, and_18_out, and_19_out);
  or or_15 (or_15_out, and_20_out, D0);
  or or_16 (g, or_8_out, or_9_out);
  or or_17 (d, or_12_out, or_13_out);
  or or_18 (f, or_14_out, or_15_out);
  _7_Segment_Display u_7_segment_display_1 (.g(g), .f(f), .a(a), .b(b), .e(e), .d(d), .c(c));  // open: dp

  // Notes on the sheet:
  //   S
  //   S
  //   S
  //   S
  //   S
  //   S
  //   S
endmodule
